# Fritzing sketch scheme (saved by Fritzing 0.9.10b)

parts:
  МК = Arduino Nano (Rev3.0)
  Сервопривод_4 = Basic Servo
  Сервопривод_3 = Basic Servo
  Вход_5V = Power plug
  Сервопривод_2 = Basic Servo
  Сервопривод_1 = Basic Servo
  Реле = RELAY [package=relay-g5q]
  Мотор_1 = DC Motor [voltage_(max)=6V voltage_(min)=3V]
  Мотор_2 = DC Motor [voltage_(max)=6V voltage_(min)=3V]
  Вход_12V = Power plug

nets:
  N1: МК.D2, Реле.COIL1
  N2: МК.D6, Сервопривод_1.pulse
  N3: МК.D9, Сервопривод_2.pulse
  N4: МК.D10, Сервопривод_3.pulse
  N5: МК.D11/MOSI, Сервопривод_4.pulse
  GND: МК.GND, Сервопривод_4.gnd, Сервопривод_3.gnd, Вход_5V.GND, Сервопривод_2.gnd, Сервопривод_1.gnd, Реле.COIL2
  VCC: Сервопривод_4.vcc, Сервопривод_3.vcc, Вход_5V.VCC, Сервопривод_2.vcc, Сервопривод_1.vcc
  N6: Реле.MAIN, Вход_12V.VCC
  N7: Реле.NO, Мотор_1.pin_1, Мотор_2.pin_1
  N8: Мотор_1.pin_2, Мотор_2.pin_2, Вход_12V.GND
